# Fritzing sketch Grupo1-Seele-Touch-Hall (saved by Fritzing 0.9.3b)
breadboards: 1

parts:
  Part1 = KY-024 Linear Hall Magnetic Sensor Module [package="Breakout board"]
  Componente1 = Arduino Uno (Rev3)

nets:
  N1: Part1.G, Componente1.GND
  N2: Part1.+, Componente1.5V
  N3: Part1.D0, Componente1.D10_PWM/SS

notes:
  KY- 036 Sensor de Tacto

custom parts:
  KY-024 Linear Hall Magnetic Sensor Module: KEYES KY-024 Arduino Linear Hall Magnetic Sensor Module reacts iin the presence of a magnetic field.
