# Fritzing sketch Grupo2_RTU (saved by Fritzing 0.9.3b)

parts:
  Componente2 = Arduino Uno (Rev3) - ICSP
  Componente3 = Thumb Joystick
  Part1 = KY-018 Photoresistor Module [package="Breakout board"]

nets:
  N1: Componente2.A0, Part1.S
  N2: Componente2.A2, Componente3.HORZ
  N3: Componente2.A3, Componente3.VERT
  N4: Componente2.D2, Componente3.SEL
  5V: Componente2.5V, Componente3.VCC
  GND: Componente2.GND, Componente3.GND, Part1.-
  VIN: Componente2.VIN, Part1.Vin

custom parts:
  KY-018 Photoresistor Module: KY-018 Photoresistor module, used to measure light intensity. It can determine the presence or absence of light.
