# Fritzing sketch Grupo4-GrupoDevs (saved by Fritzing 0.8.7b)
breadboards: 1

parts:
  Componente2 = KY-033 Tracing Black White Line Hunting Sensor Module For Arduino
  Componente1 = Arduino Uno (Rev3)
  S1 = KY-026

nets:
  GND: Componente2.GND, Componente1.GND, S1.pin2
  N1: Componente2.V+, S1.pin3
  N2: Componente2.S, Componente1.A0
  N3: Componente1.A1, S1.pin1

custom parts:
  KY-033 Tracing Black White Line Hunting Sensor Module For Arduino: Tracing Black White Line Hunting Sensor Module For Arduino Description: This is KY-033 tracking sensor. The KY-033 measures the intensity of infrared radiation and delivers it as an analog output voltage. Features: Operating voltage: 2.5 - 12V(cannot over12V) working current: 18mA-20mA at 5V Enhanced accuracy Documents: http://www.vishay.com/docs/83760/tcrt5000.pdf
  KY-026: ky-026 flame sensor module
