# Fritzing sketch Grupo5-CtrlF5 (saved by Fritzing 0.9.3b)
breadboards: 1

parts:
  Componente1 = Arduino Mega ADK (Rev3)
  hc-sr1 = hc-sr04
  Componente2 = KY-033 Tracing Black White Line Hunting Sensor Module For Arduino

nets:
  5V: Componente1.5V, hc-sr1.VCC, Componente2.V+
  GND: Componente1.GND, hc-sr1.GND, Componente2.GND
  N1: Componente1.D2_PWM, hc-sr1.Echo
  N2: Componente1.D3_PWM, hc-sr1.Trig
  N3: Componente1.D4_PWM, Componente2.S

custom parts:
  KY-033 Tracing Black White Line Hunting Sensor Module For Arduino: Tracing Black White Line Hunting Sensor Module For Arduino Description: This is KY-033 tracking sensor. The KY-033 measures the intensity of infrared radiation and delivers it as an analog output voltage. Features: Operating voltage: 2.5 - 12V(cannot over12V) working current: 18mA-20mA at 5V Enhanced accuracy Documents: http://www.vishay.com/docs/83760/tcrt5000.pdf
