# Fritzing sketch Grupo6-Groupduino (saved by Fritzing 0.9.3b)
breadboards: 1

parts:
  Componente1 = Arduino Uno (Rev3)
  Componente2 = Soil Moisture Sensor
  FC-1 = Sound Sensor

nets:
  N1: Componente1.A0, FC-1.OUT
  N2: Componente1.A1, Componente2.SIG
  VCC: Componente1.5V, Componente2.VCC, FC-1.VCC
  GND: Componente1.GND, Componente2.GND, FC-1.GND
