# Fritzing sketch Grupo7-Controllers (saved by Fritzing 0.9.3b)
breadboards: 1

parts:
  Componente1 = Arduino Uno (Rev3)
  T1 = LM35 Temperature Sensor [package="TO92 [THT]"]
  S1 = Tilt Switch [package=THT]
  R1 = Resistor [tolerance=±5% resistance=220 package="0805 [SMD]"]

nets:
  N1: Componente1.A0, T1.Vout
  GND: Componente1.GND, T1.GND, S1.Pin_1
  N2: Componente1.D2, S1.Pin_2, R1.Pin_0
  N3: Componente1.5V, T1.+Vs, R1.Pin_1

// code stored in the sketch: Grupo7-Controllers.ino
// Grupo 7: Enrique, Zaracho, Zimmermann

#include <Wire.h>

void setup()
{
  Wire.begin(6); //PONER EL Nº DE GRUPO - 1 => PARA EL GRUPO 1 VA 0
  Wire.onRequest(sendData);
  Serial.begin(9600);
}

void loop()
{
  delay(10);
}

void sendData(int howMany)
{
  int temp = analogRead(A0); //SENSOR 1 - analógico - Temperatura
  int value1 = (temp * 5 * 100) / 1024;
  char data[4];
  sprintf(data, "%0.4d", value1);
  for (int i = 0; i<4; i++) {
    Wire.write(data[i]);
  }

  int value2 = digitalRead(2); //SENSOR 2 - digital - inclinación
  sprintf(data, "%0.4d", value2);
  for (int i = 0; i<4; i++) {
    Wire.write(data[i]);
  }
}
