# Fritzing sketch Grupo8-Noxus-Reed-IRSensor (saved by Fritzing 0.9.3b)
breadboards: 1

parts:
  Componente1 = Arduino Uno (Rev3)
  Componente2 = Arduino Uno (Rev3)
  Part1 = KY-025 Reed Switch Module [package="Breakout board"]
  Part2 = KY-022 Infrared Receiver Module [package="Breakout board"]

nets:
  N1: Componente1.A4/SDA, Componente2.A4/SDA
  N2: Componente1.A5/SCL, Componente2.A5/SCL
  N3: Componente1.D2, Part2.Vin
  N4: Componente1.D3_PWM, Part1.D0
  5V: Componente1.5V, Componente2.5V, Part1.+, Part2.S
  GND: Componente1.GND, Componente2.GND, Part1.G, Part2.-

custom parts:
  KY-025 Reed Switch Module: KEYES KY-025 Arduino Reed Switch Module reacts iin the presence of a magnetic field.
  KY-022 Infrared Receiver Module: Arduino IR receiver module KY-022, reacts to 38kHz infrared light.
