# Fritzing sketch grupo 3 - Ni Idea (saved by Fritzing 0.9.3b)
breadboards: 1

parts:
  Componente1 = Arduino Mega 2560 (Rev3)
  LED2 = smd LED [color="Red (633nm)" package="0603 [SMD]"]
  U1 = IRRECEIVER [package=tsop8523]
  R1 = Resistor [tolerance=±5% resistance=220 package="0805 [SMD]"]
  J2 = Infrared Proximity Sensor

nets:
  N1: Componente1.A0, U1.GND1
  N2: Componente1.D10_PWM, J2.Vcc
  N3: Componente1.D9_PWM, R1.Pin_1
  N4: Componente1.5V, U1.OUT, J2.Vout
  GND: Componente1.GND, LED2.cathode, U1.GND2, J2.GND
  N5: LED2.anode, R1.Pin_0
